// Logisim project LOGISIM EXAM.circ as structural Verilog: 1 circuit, main circuit main
module main (
  input  in_1,
  input  [1:0] XOGADOR_1,
  input  [1:0] XOGADOR_2
);

  wire and_1_out, and_2_out, and_3_out, and_4_out, and_5_out, and_6_out, CLK, comparator_1_eq,
       comparator_2_eq, comparator_3_eq, comparator_4_eq, comparator_5_eq, comparator_6_eq, comparator_7_eq,
       comparator_8_eq, comparator_9_eq, comparator_10_eq, comparator_11_eq, comparator_12_eq,
       comparator_13_eq, MAX_PARTIDAS, VITORIA_XOGADOR_1, VITORIA_XOGADOR_2;
  wire [3:0] PARTIDA, SUM_PARTIDA, SUM_VITORIAS1, SUM_VITORIAS2, VITORIAS_TOTAIS_1, VITORIAS_TOTAIS_2;

  Clock clock_1 (.out(CLK));
  Comparator #(.width(2), .mode("unsigned")) comparator_1 (
    .a(XOGADOR_1), .b(2'b00), .eq(comparator_1_eq));  // open: gt, lt
  Comparator #(.width(2), .mode("unsigned")) comparator_2 (
    .a(XOGADOR_2), .b(2'b10), .eq(comparator_2_eq));  // open: gt, lt
  Comparator #(.width(2), .mode("unsigned")) comparator_3 (
    .a(XOGADOR_1), .b(2'b01), .eq(comparator_3_eq));  // open: gt, lt
  Comparator #(.width(2), .mode("unsigned")) comparator_4 (
    .a(XOGADOR_2), .b(2'b00), .eq(comparator_4_eq));  // open: gt, lt
  Comparator #(.width(2), .mode("unsigned")) comparator_5 (
    .a(XOGADOR_1), .b(2'b10), .eq(comparator_5_eq));  // open: gt, lt
  Comparator #(.width(2), .mode("unsigned")) comparator_6 (
    .a(XOGADOR_2), .b(2'b01), .eq(comparator_6_eq));  // open: gt, lt
  and and_1 (and_1_out, comparator_1_eq, comparator_2_eq);
  or or_1 (VITORIA_XOGADOR_1, and_1_out, and_2_out, and_3_out);
  and and_2 (and_2_out, comparator_3_eq, comparator_4_eq);
  and and_3 (and_3_out, comparator_5_eq, comparator_6_eq);
  Comparator #(.width(4), .mode("unsigned")) comparator_7 (
    .a(PARTIDA), .b(4'b1110), .eq(comparator_7_eq));  // open: gt, lt
  not not_1 (MAX_PARTIDAS, comparator_7_eq);
  Adder #(.width(4)) adder_1 (.a({3'b000, CLK}), .b(PARTIDA), .out(SUM_PARTIDA));  // open: cin, cout
  Comparator #(.width(2), .mode("unsigned")) comparator_8 (
    .a(XOGADOR_1), .b(2'b00), .eq(comparator_8_eq));  // open: gt, lt
  Comparator #(.width(2), .mode("unsigned")) comparator_9 (
    .a(XOGADOR_2), .b(2'b01), .eq(comparator_9_eq));  // open: gt, lt
  Comparator #(.width(2), .mode("unsigned")) comparator_10 (
    .a(XOGADOR_1), .b(2'b01), .eq(comparator_10_eq));  // open: gt, lt
  Comparator #(.width(2), .mode("unsigned")) comparator_11 (
    .a(XOGADOR_2), .b(2'b10), .eq(comparator_11_eq));  // open: gt, lt
  Comparator #(.width(2), .mode("unsigned")) comparator_12 (
    .a(XOGADOR_1), .b(2'b10), .eq(comparator_12_eq));  // open: gt, lt
  Comparator #(.width(2), .mode("unsigned")) comparator_13 (
    .a(XOGADOR_2), .b(2'b00), .eq(comparator_13_eq));  // open: gt, lt
  and and_4 (and_4_out, comparator_8_eq, comparator_9_eq);
  and and_5 (and_5_out, comparator_10_eq, comparator_11_eq);
  and and_6 (and_6_out, comparator_12_eq, comparator_13_eq);
  Counter #(.width(4), .max('hf)) counter_1 (
    .D(SUM_PARTIDA), .count(MAX_PARTIDAS), .Q(PARTIDA), .clk(CLK), .clr(in_1));  // open: load, carry
  or or_2 (VITORIA_XOGADOR_2, and_4_out, and_5_out, and_6_out);
  // Probe on PARTIDA
  Register #(.width(4)) register_1 (.D(SUM_VITORIAS1), .en(MAX_PARTIDAS), .Q(VITORIAS_TOTAIS_1), .clk(CLK), .clr(in_1));
  Register #(.width(4)) register_2 (.D(SUM_VITORIAS2), .en(MAX_PARTIDAS), .Q(VITORIAS_TOTAIS_2), .clk(CLK), .clr(in_1));
  Adder #(.width(4)) adder_2 (
    .a({3'b000, VITORIA_XOGADOR_1}), .b(VITORIAS_TOTAIS_1), .out(SUM_VITORIAS1));  // open: cin, cout
  // Probe on VITORIAS_TOTAIS_1
  Adder #(.width(4)) adder_3 (
    .a({3'b000, VITORIA_XOGADOR_2}), .b(VITORIAS_TOTAIS_2), .out(SUM_VITORIAS2));  // open: cin, cout
  // Probe on VITORIAS_TOTAIS_2

  // Other names for the same wires on the sheet: _1[1:0] = XOGADOR_1; _2[1:0] = XOGADOR_2; RST = in_1

  // Notes on the sheet:
  //   Deseño dixital - 1ª oportunidade - 12/06/2020
  //   JOAQUÍN SOLLA VÁZQUEZ
endmodule
