// Logisim project Modulos.circ as structural Verilog: 1 circuit, main circuit main
module main (
  input  in_1
);

  wire A_B, Ciclo_7, CLK, comparator_3_eq;
  wire [0:0] adder_1_out;
  wire [2:0] cont_condicion, counter_2_q;
  wire [3:0] A, A_B__2, A_B___A_B, B, Ciclo, not_1_out, register_2_q, X, xor_1_out, Y;

  Adder #(.width(4)) adder_1 (.a(A), .b(B), .out({A_B__2[2:0], adder_1_out[0]}), .cout(A_B__2[3]));  // open: cin
  Register #(.width(4)) register_1 (.D(A), .en(A_B), .Q(B), .clk(CLK));  // open: clr
  Comparator #(.width(4), .mode("unsigned")) comparator_1 (.a(A), .b(B), .gt(A_B));  // open: eq, lt
  assign xor_1_out = B ^ {4{in_1}};  // XOR_Gate xor_1, 4 bits wide
  Comparator #(.width(4), .mode("unsigned")) comparator_2 (.a({B[3], A[2:0]}), .b({A[3], B[2:0]}));  // open: gt, eq, lt
  Adder #(.width(4)) adder_2 (.a(A), .b(xor_1_out), .out(A_B___A_B), .cin(in_1));  // open: cout
  // Probe on xor_1_out
  // Probe on cont_condicion
  Counter #(.width(3), .max('h7)) counter_1 (.count(A_B), .Q(cont_condicion), .clk(CLK));  // open: load, D, carry, clr
  Clock clock_1 (.out(CLK));
  Register #(.width(4)) register_2 (.D(X), .Q(register_2_q), .clk(CLK));  // open: en, clr
  not not_1 (not_1_out[0], register_2_q[0]);
  not not_2 (not_1_out[1], register_2_q[1]);
  not not_3 (not_1_out[2], register_2_q[2]);
  not not_4 (not_1_out[3], register_2_q[3]);
  Counter #(.width(3), .max('h7)) counter_2 (.load(Ciclo_7), .Q(counter_2_q), .clk(CLK));  // open: D, count, carry, clr
  Adder #(.width(4)) adder_3 (.a(not_1_out), .b(X), .out(Y), .cin(1'b1));  // open: cout
  and and_1 (Ciclo_7, counter_2_q[1], counter_2_q[2]);
  Comparator #(.width(4), .mode("unsigned")) comparator_3 (
    .a({Ciclo[3], 3'b001}), .b({1'b0, Ciclo[2:0]}), .eq(comparator_3_eq));  // open: gt, lt
  Register #(.width(4)) register_3 (.D(X), .en(comparator_3_eq), .Q(A), .clk(CLK));  // open: clr
  // Probe on A

  // Other names for the same wires on the sheet: minus_S__R = in_1; MAX[3:0] = B; A_prime[4:0] = {{2{A[3]}}, A[2:0]};
  //   Ciclo_prime[2:0] = Ciclo[2:0]; Constante1_prime[3] = Ciclo[3]

  // Notes on the sheet:
  //   Calcula la media de dos nº de 4 bits en BP
  //   Compara dos nº en C2
  //   Sumador/restador
  //   Cuenta el nº de veces que se cumple una condición
  //   (en este caso A>B)
  //   Muestra el maximo de todos los valores recibidos hasta el momento
  //   Entra x en BP. Resta el x actual y el anterior y lo expresa en C2
  //   Contador modulo 7 con salida carry
  //   Extension de signo
  //   Detecta el ciclo igual a la constante en C2
  //   (en este caso el primer ciclo)
  //   Salida carry
endmodule
