// Logisim project PD0.circ as structural Verilog: 1 circuit, main circuit main
module main (
);

  wire adder_1_cout, adder_2_cout;
  wire [3:0] A_B, A_B_1, multiplexer_1_out, not_1_out;

  assign not_1_out = ~4'b0001;  // NOT_Gate not_1, 4 bits wide
  Multiplexer #(.width(4), .disabled(0), .enable("false")) multiplexer_1 (
    .in0(A_B), .in1(A_B_1), .out(multiplexer_1_out), .sel(1'b1));
  Adder #(.width(4)) adder_1 (.a(4'b1010), .b(4'b1011), .out(A_B), .cout(adder_1_cout));  // open: cin
  // Probe on adder_1_cout
  Adder #(.width(4)) adder_2 (.a(A_B), .b(not_1_out), .out(A_B_1), .cin(1'b1), .cout(adder_2_cout));
  // Probe on adder_2_cout
  // Probe on multiplexer_1_out
  // Probe on A_B
  // Probe on A_B_1

  // Notes on the sheet:
  //   SUMA A+B
  //   SUMA (A+B-1)
  //   SELECTOR
endmodule
