// Logisim project PD1.circ as structural Verilog: 1 circuit, main circuit main
module main (
);

  wire comparator_1_lt;
  wire [3:0] not_1_out;
  wire [5:0] _2__B_C, B_A, B_C, Y;

  // Probe on 4'b0101
  // Probe on 4'b0001
  // Probe on 4'b0010
  // Probe on Y
  // Probe on Y
  Comparator #(.width(6), .mode("unsigned")) comparator_1 (
    .a(6'b000101), .b(B_C), .lt(comparator_1_lt));  // open: gt, eq
  assign not_1_out = ~4'b0101;  // NOT_Gate not_1, 4 bits wide
  Adder #(.width(6)) adder_1 (.a(B_C), .b(B_C), .out(_2__B_C));  // open: cin, cout
  Adder #(.width(4)) adder_2 (.a(4'b0001), .b(not_1_out), .out({B_A[5], B_A[2:0]}), .cin(1'b1));  // open: cout
  Multiplexer #(.width(6), .disabled(0), .enable("false")) multiplexer_1 (
    .in0({{3{B_A[5]}}, B_A[2:0]}), .in1(_2__B_C), .out(Y), .sel(comparator_1_lt));
  Adder #(.width(6)) adder_3 (.a(6'b000001), .b(6'b000010), .out(B_C));  // open: cin, cout

  // Other names for the same wires on the sheet: B_A[4:3] = {2{B_A[5]}}

  // Notes on the sheet:
  //   6 bits
endmodule
