// Logisim project PD2.circ as structural Verilog: 1 circuit, main circuit main
module main (
  input  [3:0] in_1
);

  wire CICLO_FINAL, CLK, CONDICION, ENABLE, IMPAR, NEGATIVO, RESET;
  wire [2:0] CONT, Y;
  wire [3:0] CICLO;

  Clock clock_1 (.out(CLK));
  // Probe on in_1
  Counter #(.width(4), .max('h7)) counter_1 (.Q(CICLO), .carry(RESET), .clk(CLK));  // open: load, D, count, clr
  // Probe on CICLO
  Comparator #(.width(4), .mode("unsigned")) comparator_1 (
    .a({1'b0, in_1[2:0]}), .b({in_1[3], 3'b000}), .lt(NEGATIVO));  // open: gt, eq
  Comparator #(.width(1), .mode("unsigned")) comparator_2 (.a(in_1[0]), .b(1'b1), .eq(IMPAR));  // open: gt, lt
  // Probe on CONDICION
  or or_1 (CONDICION, NEGATIVO, IMPAR);
  Comparator #(.width(4), .mode("unsigned")) comparator_3 (.a(CICLO), .b(4'b0111), .eq(CICLO_FINAL));  // open: gt, lt
  // Probe on ENABLE
  and and_1 (ENABLE, CONDICION, CICLO_FINAL);
  // Probe on CONT
  Counter #(.width(3), .max('h6)) counter_2 (
    .count(CONDICION), .Q(CONT), .clk(CLK), .clr(RESET));  // open: load, D, carry
  // Probe on CONT
  Register #(.width(3)) register_1 (.D(CONT), .en(ENABLE), .Q(Y), .clk(CLK), .clr(RESET));
  // Probe on Y

  // Other names for the same wires on the sheet: X[3:0] = in_1

  // Notes on the sheet:
  //   Deseña e implementa usando o programa LogiSim un circuíto secuencial que reciba por
  //   unha entrada X (de 4 bits en complemento a 2) secuencias de 7 valores (un por ciclo) e
  //   conte cantas veces se cumple que o número é negativo ou impar. No oitavo ciclo
  //   mostrarase o valor da conta pola saída Y do circuíto (de 3 bits en binario puro) e non se
  //   usará o valor da entrada X.
endmodule
