// Logisim project vending_machine.circ as structural Verilog: 1 circuit, main circuit main
module main (
  input  A,
  input  B,
  input  _0_5,
  input  _1,
  input  _2
);

  wire CLK, CLK_AB, CLK_t, comparator_1_eq, comparator_2_eq, comparator_3_eq, comparator_3_gt,
       comparator_4_eq, comparator_4_gt, comparator_5_eq, comparator_6_eq, EMPTY, ENABLE, END_A, END_B,
       multiplexer_4_out, multiplexer_5_out, multiplexer_6_out, NEW, nor_1_out, not_1_out, not_2_out,
       or_3_out, or_4_out, or_5_out, RST;
  wire [1:0] C_CNTRL, multiplexer_1_out;
  wire [8:0] ADD, INSRTD, SUM;

  Clock u_RST (.out(RST));
  Clock u_NEW (.out(NEW));
  Multiplexer #(.width(2), .disabled(0), .enable("false")) multiplexer_1 (
    .in0(2'b01), .in1(2'b10), .out(multiplexer_1_out), .sel(_1));
  Multiplexer #(.width(2), .disabled(0), .enable("false")) multiplexer_2 (
    .in0(multiplexer_1_out), .in1(2'b11), .out(C_CNTRL), .sel(_2));
  // Probe on ADD
  Multiplexer #(.select(2), .width(9), .disabled(0), .enable("false")) multiplexer_3 (
    .in0({9{1'b0}}), .in1(9'h32), .in2(9'h64), .in3(9'hc8), .out(ADD), .sel(C_CNTRL));
  // Probe on C_CNTRL
  // Probe on SUM
  Adder #(.width(9)) adder_1 (.a(ADD), .b(INSRTD), .out(SUM));  // open: cin, cout
  or or_1 (CLK, _0_5, _1, _2);
  or or_2 (CLK_AB, A, B);
  Comparator #(.width(9), .mode("unsigned")) comparator_1 (
    .a(INSRTD), .b(9'h96), .eq(comparator_1_eq));  // open: gt, lt
  Multiplexer #(.disabled(0), .enable("false")) multiplexer_4 (
    .in0(1'b1), .in1(1'b0), .out(multiplexer_4_out), .sel(comparator_1_eq));
  Comparator #(.width(9), .mode("unsigned")) comparator_2 (
    .a(INSRTD), .b(9'hc8), .eq(comparator_2_eq));  // open: gt, lt
  Comparator #(.width(9), .mode("unsigned")) comparator_3 (
    .a(INSRTD), .b(9'h64), .gt(comparator_3_gt), .eq(comparator_3_eq));  // open: lt
  Comparator #(.width(9), .mode("unsigned")) comparator_4 (
    .a(INSRTD), .b(9'h96), .gt(comparator_4_gt), .eq(comparator_4_eq));  // open: lt
  Multiplexer #(.disabled(0), .enable("false")) multiplexer_5 (
    .in0(multiplexer_4_out), .in1(1'b0), .out(multiplexer_5_out), .sel(comparator_2_eq));
  and and_1 (END_A, A, or_3_out);
  or or_3 (or_3_out, comparator_3_gt, comparator_3_eq);
  and and_2 (END_B, B, or_4_out);
  or or_4 (or_4_out, comparator_4_gt, comparator_4_eq);
  Multiplexer #(.disabled(0), .enable("false")) multiplexer_6 (
    .in0(multiplexer_5_out), .in1(1'b0), .out(multiplexer_6_out), .sel(comparator_5_eq));
  Comparator #(.width(9), .mode("unsigned")) comparator_5 (
    .a(INSRTD), .b(9'hfa), .eq(comparator_5_eq));  // open: gt, lt
  // Probe on END_A
  // Probe on END_B
  Multiplexer #(.disabled(0), .enable("false")) multiplexer_7 (
    .in0(multiplexer_6_out), .in1(1'b0), .out(ENABLE), .sel(comparator_6_eq));
  Comparator #(.width(9), .mode("unsigned")) comparator_6 (
    .a(INSRTD), .b(9'h12c), .eq(comparator_6_eq));  // open: gt, lt
  Register #(.width(9)) register_1 (.D(SUM), .en(ENABLE), .Q(INSRTD), .clk(not_1_out), .clr(or_5_out));
  not not_1 (not_1_out, CLK_t);
  nor nor_1 (nor_1_out, END_A, END_B);
  not not_2 (not_2_out, CLK_AB);
  // Probe on INSRTD
  or or_5 (or_5_out, EMPTY, RST);
  Register #(.width(1)) register_2 (.D(nor_1_out), .Q(EMPTY), .clk(not_2_out), .clr(NEW));  // open: en

  // Notes on the sheet:
  //   al consumidor.
  //   dinero insertado se hará lo siguiente:
  //   y la máquina guarda el dinero.
  //   seguirá almacenanso nuevas monedas.
  //   ADD COIN TO INSERTED
  //   La máquina acepta monedas de 50 céntimos y de 1 y 2 euros.
  //   -Si tiene menos dinero del necesario, este se devolverá.
  //   -Si tiene el dinero suficiente, se proporciona el producto indicado
  //   COIN CONTROL
  //   Una máquina expendedora dispone de dos productos (A y B), de valor 1€ y 1.5€ respectivamente.
  //   Para elegir uno de los productos se pulsa el botón (botón A obotón B) y dependiendo del
  //   Además, posee un botón RESET que devolverá el dinero introducido en caso de no comprar nada.
  //   La máquina no podrá contener un importe mayor a 3€, pero si ya ha superado los 1.5€, tampoco
  //   (Suopnemos que solo se puede pulsar un botón o introducir una moneda de cada vez).
  //   (En esta máquina, si se inserta más dinero del que cuesta el producto, este no se devolverá
  //   2 CLOCKS
  //   A CONTROL
  //   B CONTROL
  //   DISABLE IF INSERTED = 150, 200, 250 o 300
  //   EMPTY COINS WHEN END A or END B
endmodule
